# Fritzing sketch FIngerprint Voting Machine (saved by Fritzing 0.9.6b)

parts:
  GT-511C1R2 = GT-511C1R Fingerprint Scanner
  Part1 = Arduino Uno (Rev3)
  LCD1 = LCD screen
  R1 = Trimmer Potentiometer [maximum_resistance=10kΩ package=THT]
  S1 = SWITCH-MOMENTARY-2 [package=tactile-pth-12mm]
  S2 = SWITCH-MOMENTARY-2 [package=tactile-pth-12mm]  # not connected
  S3 = SWITCH-MOMENTARY-2 [package=tactile-pth-12mm]  # not connected
  S4 = SWITCH-MOMENTARY-2 [package=tactile-pth-12mm]  # not connected
  S5 = SWITCH-MOMENTARY-2 [package=tactile-pth-12mm]
  S6 = SWITCH-MOMENTARY-2 [package=tactile-pth-12mm]
  S7 = SWITCH-MOMENTARY-2 [package=tactile-pth-12mm]  # not connected
  S8 = SWITCH-MOMENTARY-2 [package=tactile-pth-12mm]  # not connected
  S9 = SWITCH-MOMENTARY-2 [package=tactile-pth-12mm]
  J1 = Piezo Speaker

nets:
  N1: GT-511C1R2.Tx, Part1.D0/RX
  N2: GT-511C1R2.Rx, Part1.D1/TX
  GND: GT-511C1R2.GND, Part1.GND, LCD1.VSS, LCD1.LED-, J1.pin1
  VIN: GT-511C1R2.Vin, Part1.5V
  N3: Part1.D8, LCD1.DB6
  N4: Part1.D9_PWM, LCD1.DB7
  N5: Part1.D3_PWM, J1.pin2
  N6: Part1.D4, LCD1.RS
  N7: Part1.D5_PWM, LCD1.E
  N8: Part1.D6_PWM, LCD1.DB4
  N9: Part1.D7, LCD1.DB5
  N10: LCD1.VDD, LCD1.LED+
  N11: LCD1.V0, R1.wiper
  N12: S1.1, S5.1
  N13: S6.1, S9.1

notes:
  enroll -10
  delete - 11
  up 12
  down 13
  match 14
  can1 15
  can2 16
  can3 17
  resultsw 18
  other pin should be grounded
  LCD 4,5,6,7,8,9
  Buzzer 3
  R305 / R307
  Fingerprint sensor
  yellow wire 0
  white wure 1
  Finger Print Voting Machine

custom parts:
  GT-511C1R Fingerprint Scanner: The GT-511C1R fingerprint scanner. The fingerprint module is produced by ADH-Tech. The GT-511C1 is based around the ARM Cortex M3 and can store 20 fingerprints.
